# Fritzing sketch 가로등 및 주차 바리게이트 (saved by Fritzing 0.9.3b)
breadboards: 1

parts:
  부품1 = Arduino Uno (Rev3)
  R1 = Resistor [tolerance=±5% power=0.25 resistance=220 package=THT]
  LED1 = LED - 3mm [color="Red (633nm)" current=0.030 package="3 mm [THT]"]
  J1 = Basic Servo
  HC-SR04_Sensor_1 = HC-SR04 Ultrasonic Distance Sensor  # not connected

nets:
  N1: 부품1.D12/MISO, LED1.anode
  N2: 부품1.D13/SCK, J1.gnd
  N3: 부품1.GND, R1.Pin_1, J1.pulse
  N4: R1.Pin_0, LED1.cathode
