# Fritzing sketch 세그먼트 신호등 (saved by Fritzing 0.9.10b)
breadboards: 1

parts:
  부품1 = Arduino Uno (Rev3)
  U1 = AD5206 Digital Potentiometer [maximum_resistance=10kΩ knob_status=50% package="DIP28 [THT]"]
  U2 = 7-SEGMENT-DISPLAY [package=7-segment-display]
  R1 = Resistor [tolerance=±5% power=0.25 resistance=220 package=THT]
  LED1 = LED - 5mm [color="Red (633nm)" current=0.030 package="5 mm [THT]"]  # not connected
  LED2 = LED - 5mm [color="Red (633nm)" current=0.030 package="5 mm [THT]"]  # not connected
  LED3 = LED - 5mm [color="Red (633nm)" current=0.030 package="5 mm [THT]"]
  R2 = Resistor [tolerance=±5% power=0.25 resistance=220 package=THT]
  R3 = Resistor [tolerance=±5% power=0.25 resistance=220 package=THT]
  R4 = Resistor [tolerance=±5% power=0.25 resistance=220 package=THT]

nets:
  N1: 부품1.D9_PWM, U1.Vdd
  N2: 부품1.D10_PWM/SS, U1.Gnd
  N3: 부품1.D11_PWM/MOSI, U1.B6
  N4: 부품1.GND, U1.CS, LED3.cathode
  N5: 부품1.D5_PWM, R4.Pin_0
  N6: 부품1.D6_PWM, R3.Pin_0
  N7: 부품1.D7, R2.Pin_0
  N8: 부품1.5V, U1.W6, U1.A5
  N9: U1.W5, U2.G2
  N10: U1.W1, U2.A
  N11: U1.A1, U2.C
  N12: U1.A2, U2.G1
  N13: U1.W2, U2.D
  N14: U1.B2, U2.G
  N15: U1.A4, U2.E
  N16: U2.F, R1.Pin_1
